// Logisim project Single Cycle Processor.circ as structural Verilog
module main (
  input  in_1
);

  wire ALUOp, ALUSrc, Clk, ExtOp, MemRd, MemWr, RegDst, RegWr, WBdata, Zero_Flag;
  wire [1:0] PCSrc;
  wire [2:0] multiplexer_2_out;
  wire [13:0] adder_1_out, adder_2_out, multiplexer_1_out, register_1_q, undriven;
  wire [15:0] ALU_p4, bit_extender_1_out, bit_extender_2_out, File_Register_busa, File_Register_busb,
       multiplexer_3_out, multiplexer_4_out, multiplexer_5_out, ram_1_data, ram_2_data;

  Multiplexer #(.select(2), .width(14), .enable("false")) multiplexer_1 (
    .in0(adder_1_out), .in1(ram_1_data[13:0]), .in2(adder_2_out), .in3(undriven), .out(multiplexer_1_out),
    .sel(PCSrc));
  Register #(.width(14)) register_1 (.D(multiplexer_1_out), .Q(register_1_q), .clk(Clk), .clr(in_1));  // open: en
  Adder #(.width(14)) adder_1 (.a(14'h2), .b(register_1_q), .out(adder_1_out));  // open: cin, cout
  Clock clock_1 (.out(Clk));
  RAM #(.addrWidth(14), .dataWidth(16)) ram_1 (
    .addr(register_1_q), .data(ram_1_data), .clk(Clk), .ld(1'b1));  // open: sel, clr
  assign bit_extender_1_out = {{10{ram_1_data[15]}}, ram_1_data[15:10]};  // Bit_Extender bit_extender_1
  assign bit_extender_2_out = {{10{1'b0}}, ram_1_data[15:10]};  // Bit_Extender bit_extender_2
  Multiplexer #(.width(3), .enable("false")) multiplexer_2 (
    .in0(ram_1_data[9:7]), .in1(ram_1_data[12:10]), .out(multiplexer_2_out), .sel(RegDst));
  Multiplexer #(.width(16), .enable("false")) multiplexer_3 (
    .in0(bit_extender_1_out), .in1(bit_extender_2_out), .out(multiplexer_3_out), .sel(ExtOp));
  File_Register File_Register (
    .BusW(multiplexer_5_out), .RegWrite(RegWr), .RA(ram_1_data[6:4]), .RB(ram_1_data[9:7]),
    .BusA(File_Register_busa), .BusB(File_Register_busb), .RW(multiplexer_2_out), .Clock(Clk));
  Adder #(.width(14)) adder_2 (.a(adder_1_out), .b(multiplexer_3_out[13:0]), .out(adder_2_out));  // open: cin, cout
  Multiplexer #(.width(16), .enable("false")) multiplexer_4 (
    .in0(File_Register_busb), .in1(multiplexer_3_out), .out(multiplexer_4_out), .sel(ALUSrc));
  // ALU ALU: pin names not known; wires that end beside it: File_Register_busa, multiplexer_4_out, ALUOp, ALU_p4, Zero_Flag
  RAM #(.addrWidth(16), .dataWidth(16), .bus("separate")) ram_2 (
    .addr(ALU_p4), .din(File_Register_busb), .data(ram_2_data), .str(MemRd), .clk(Clk), .ld(MemWr));  // open: sel, clr
  Multiplexer #(.width(16), .enable("false")) multiplexer_5 (
    .in0(ALU_p4), .in1(ram_2_data), .out(multiplexer_5_out), .sel(WBdata));
  // Pins of 14 and 16 bits meet at ram_1_data
  // Pins of 14 and 16 bits meet at 16'h2
  // Pins of 14 and 16 bits meet at multiplexer_3_out
endmodule

module ALU (
  input  [3:0] ALUOp,
  input  [2:0] A,
  input  [2:0] B,
  output ZeroFlag
);

  wire [2:0] adder_1_out, and_1_out, multiplexer_1_out, not_1_out, or_1_out, shifter_1_out, shifter_2_out,
       shifter_3_out, shifter_4_out, subtractor_1_out, xor_1_out;

  assign or_1_out = A | B;  // OR_Gate or_1, 3 bits wide
  assign not_1_out = ~and_1_out;  // NOT_Gate not_1, 3 bits wide
  assign and_1_out = A & B;  // AND_Gate and_1, 3 bits wide
  assign xor_1_out = A ^ B;  // XOR_Gate xor_1, 3 bits wide
  Adder #(.width(3)) adder_1 (.a(A), .b(B), .out(adder_1_out));  // open: cin, cout
  Subtractor #(.width(3)) subtractor_1 (.a(A), .b(B), .out(subtractor_1_out));  // open: bin, bout
  Shifter_part #(.width(3)) shifter_1 (.in(A), .\dist (B[1:0]), .out(shifter_1_out));
  Shifter_part #(.width(3), .shift("lr")) shifter_2 (.in(A), .\dist (B[1:0]), .out(shifter_2_out));
  Shifter_part #(.width(3), .shift("ar")) shifter_3 (.in(A), .\dist (B[1:0]), .out(shifter_3_out));
  Shifter_part #(.width(3), .shift("rr")) shifter_4 (.in(A), .\dist (B[1:0]), .out(shifter_4_out));
  Multiplexer #(.select(4), .width(3), .enable("false")) multiplexer_1 (
    .in0(or_1_out), .in1(and_1_out), .in2(not_1_out), .in3(xor_1_out), .in4(adder_1_out),
    .in5(subtractor_1_out), .in6(shifter_1_out), .in7(shifter_2_out), .in8(shifter_3_out),
    .in9(shifter_4_out), .out(multiplexer_1_out), .sel(ALUOp));  // open: in10, in11, in12, in13, in14, in15
  Comparator #(.width(3)) comparator_1 (.a(3'b000), .b(subtractor_1_out), .eq(ZeroFlag));  // open: gt, lt
  // Pins of 2 and 3 bits meet at B
endmodule

module Shifter (
  input  [15:0] Data,
  input  [3:0] Shift_amount,
  input  [1:0] Shift_Op,
  output [15:0] Data_out
);

  wire [15:0] shifter_1_out, shifter_2_out, shifter_3_out, shifter_4_out;

  Shifter_part #(.width(16)) shifter_1 (.in(Data), .\dist (Shift_amount), .out(shifter_1_out));
  Shifter_part #(.width(16), .shift("lr")) shifter_2 (.in(Data), .\dist (Shift_amount), .out(shifter_2_out));
  Shifter_part #(.width(16), .shift("ar")) shifter_3 (.in(Data), .\dist (Shift_amount), .out(shifter_3_out));
  Shifter_part #(.width(16), .shift("rr")) shifter_4 (.in(Data), .\dist (Shift_amount), .out(shifter_4_out));
  Multiplexer #(.select(2), .width(16), .enable("false")) multiplexer_1 (
    .in0(shifter_1_out), .in1(shifter_2_out), .in2(shifter_3_out), .in3(shifter_4_out), .out(Data_out),
    .sel(Shift_Op));
endmodule

module File_Register (
  input  [2:0] RA,
  input  [2:0] RB,
  input  [2:0] RW,
  input  [15:0] BusW,
  input  RegWrite,
  input  Clock,
  output [15:0] BusA,
  output [15:0] BusB
);

  wire and_1_out, and_2_out, and_3_out, and_4_out, and_5_out, and_6_out, and_7_out, decoder_1_out0,
       decoder_1_out1, decoder_1_out2, decoder_1_out3, decoder_1_out4, decoder_1_out5, decoder_1_out6,
       decoder_1_out7, decoder_2_out0, decoder_2_out1, decoder_2_out2, decoder_2_out3, decoder_2_out4,
       decoder_2_out5, decoder_2_out6, decoder_2_out7, decoder_3_out0, decoder_3_out1, decoder_3_out2,
       decoder_3_out3, decoder_3_out4, decoder_3_out5, decoder_3_out6, decoder_3_out7;
  wire [15:0] R1_q, R2_q, R3_q, R4_q, R5_q, R6_q;

  Decoder #(.select(3), .enable("false")) decoder_1 (
    .out0(decoder_1_out0), .out1(decoder_1_out1), .out2(decoder_1_out2), .out3(decoder_1_out3),
    .out4(decoder_1_out4), .out5(decoder_1_out5), .out6(decoder_1_out6), .out7(decoder_1_out7), .sel(RW));
  Register #(.width(16)) R1 (.D(BusW), .en(and_1_out), .Q(R1_q), .clk(Clock));  // open: clr
  and and_1 (and_1_out, decoder_1_out1, RegWrite);
  Register #(.width(16)) R2 (.D(BusW), .en(and_2_out), .Q(R2_q), .clk(Clock));  // open: clr
  and and_2 (and_2_out, decoder_1_out2, RegWrite);
  Register #(.width(16)) R3 (.D(BusW), .en(and_3_out), .Q(R3_q), .clk(Clock));  // open: clr
  and and_3 (and_3_out, decoder_1_out3, RegWrite);
  Register #(.width(16)) R4 (.D(BusW), .en(and_4_out), .Q(R4_q), .clk(Clock));  // open: clr
  and and_4 (and_4_out, decoder_1_out4, RegWrite);
  Register #(.width(16)) R5 (.D(BusW), .en(and_5_out), .Q(R5_q), .clk(Clock));  // open: clr
  and and_5 (and_5_out, decoder_1_out5, RegWrite);
  Register #(.width(16)) R6 (.D(BusW), .en(and_6_out), .Q(R6_q), .clk(Clock));  // open: clr
  and and_6 (and_6_out, decoder_1_out6, RegWrite);
  Register #(.width(16)) R7 (.D(BusW), .en(and_7_out), .Q(BusA), .clk(Clock));  // open: clr
  and and_7 (and_7_out, decoder_1_out7, RegWrite);
  Decoder #(.select(3), .enable("false")) decoder_2 (
    .out0(decoder_2_out0), .out1(decoder_2_out1), .out2(decoder_2_out2), .out3(decoder_2_out3),
    .out4(decoder_2_out4), .out5(decoder_2_out5), .out6(decoder_2_out6), .out7(decoder_2_out7), .sel(RA));
  assign BusA = decoder_2_out1 ? R1_q : 16'bz;  // Controlled_Buffer controlled_buffer_1
  assign BusA = decoder_2_out2 ? R2_q : 16'bz;  // Controlled_Buffer controlled_buffer_2
  assign BusA = decoder_2_out3 ? R3_q : 16'bz;  // Controlled_Buffer controlled_buffer_3
  assign BusA = decoder_2_out4 ? R4_q : 16'bz;  // Controlled_Buffer controlled_buffer_4
  assign BusA = decoder_2_out5 ? R5_q : 16'bz;  // Controlled_Buffer controlled_buffer_5
  assign BusA = decoder_2_out6 ? R6_q : 16'bz;  // Controlled_Buffer controlled_buffer_6
  assign BusA = decoder_2_out7 ? BusA : 16'bz;  // Controlled_Buffer controlled_buffer_7
  assign BusA = decoder_2_out0 ? {16{1'b0}} : 16'bz;  // Controlled_Buffer controlled_buffer_8
  Decoder #(.select(3), .enable("false")) decoder_3 (
    .out0(decoder_3_out0), .out1(decoder_3_out1), .out2(decoder_3_out2), .out3(decoder_3_out3),
    .out4(decoder_3_out4), .out5(decoder_3_out5), .out6(decoder_3_out6), .out7(decoder_3_out7), .sel(RB));
  assign BusB = decoder_3_out0 ? {16{1'b0}} : 16'bz;  // Controlled_Buffer controlled_buffer_9
  assign BusB = decoder_3_out1 ? R1_q : 16'bz;  // Controlled_Buffer controlled_buffer_10
  assign BusB = decoder_3_out2 ? R2_q : 16'bz;  // Controlled_Buffer controlled_buffer_11
  assign BusB = decoder_3_out3 ? R3_q : 16'bz;  // Controlled_Buffer controlled_buffer_12
  assign BusB = decoder_3_out4 ? R4_q : 16'bz;  // Controlled_Buffer controlled_buffer_13
  assign BusB = decoder_3_out5 ? R5_q : 16'bz;  // Controlled_Buffer controlled_buffer_14
  assign BusB = decoder_3_out6 ? R6_q : 16'bz;  // Controlled_Buffer controlled_buffer_15
  assign BusB = decoder_3_out7 ? BusA : 16'bz;  // Controlled_Buffer controlled_buffer_16
endmodule

module Control_Unit (
);

  PC_Control pc_control_1 ();
endmodule
